// Logisim project moving_words_circuit.circ as structural Verilog: 7 circuits, main circuit main
module main (
);

  wire button_1_out, main_machine_1_indicator;
  wire [6:0] main_machine_1_out_4, main_machine_1_out_5, main_machine_1_out_6, main_machine_1_out_7,
       main_machine_1_out_8, main_machine_1_out_9, main_machine_1_out_10, main_machine_1_out_11,
       main_machine_1_out_12, main_machine_1_out_13, main_machine_1_out_14, main_machine_1_out_15,
       main_machine_1_out_16, main_machine_1_out_17, main_machine_1_out_18, main_machine_1_out_19,
       main_machine_1_out_20, main_machine_1_out_21, main_machine_1_out_22, main_machine_1_out_23,
       main_machine_1_out_24, main_machine_1_out_25, main_machine_1_out_26, main_machine_1_out_27,
       main_machine_1_out_28, main_machine_1_out_29, main_machine_1_out_30, main_machine_1_out_31,
       main_machine_1_out_32, main_machine_1_out_33, main_machine_1_out_34, main_machine_1_out_35,
       main_machine_1_out_36, main_machine_1_out_37, main_machine_1_out_38, main_machine_1_out_39,
       main_machine_1_out_40, main_machine_1_out_41, main_machine_1_out_42, main_machine_1_out_43,
       main_machine_1_out_44, main_machine_1_out_45, main_machine_1_out_46, main_machine_1_out_47,
       main_machine_1_out_48, main_machine_1_out_49, main_machine_1_out_50, main_machine_1_out_51,
       main_machine_1_out_52, main_machine_1_out_53, main_machine_1_out_54, main_machine_1_out_55,
       main_machine_1_out_56, main_machine_1_out_57, main_machine_1_out_58, main_machine_1_out_59,
       main_machine_1_out_60, main_machine_1_out_61, main_machine_1_out_62, main_machine_1_out_63,
       main_machine_1_out_64, main_machine_1_out_65, main_machine_1_out_66, main_machine_1_out_67;
  wire [7:0] rom_1_data;
  wire [16:0] main_machine_1_memory_address;

  Button button_1 (.out(button_1_out));
  LED led_1 (.in(main_machine_1_indicator));
  main_machine main_machine_1 (
    .ON_OFF_BUTTON(button_1_out), .INDICATOR(main_machine_1_indicator), .out_4(main_machine_1_out_4),
    .out_5(main_machine_1_out_5), .out_6(main_machine_1_out_6), .out_7(main_machine_1_out_7),
    .out_8(main_machine_1_out_8), .out_9(main_machine_1_out_9), .out_10(main_machine_1_out_10),
    .out_11(main_machine_1_out_11), .out_12(main_machine_1_out_12), .out_13(main_machine_1_out_13),
    .out_14(main_machine_1_out_14), .out_15(main_machine_1_out_15), .out_16(main_machine_1_out_16),
    .out_17(main_machine_1_out_17), .out_18(main_machine_1_out_18), .out_19(main_machine_1_out_19),
    .out_20(main_machine_1_out_20), .out_21(main_machine_1_out_21), .out_22(main_machine_1_out_22),
    .out_23(main_machine_1_out_23), .out_24(main_machine_1_out_24), .out_25(main_machine_1_out_25),
    .out_26(main_machine_1_out_26), .out_27(main_machine_1_out_27), .out_28(main_machine_1_out_28),
    .out_29(main_machine_1_out_29), .out_30(main_machine_1_out_30), .out_31(main_machine_1_out_31),
    .out_32(main_machine_1_out_32), .out_33(main_machine_1_out_33), .out_34(main_machine_1_out_34),
    .out_35(main_machine_1_out_35), .out_36(main_machine_1_out_36), .out_37(main_machine_1_out_37),
    .out_38(main_machine_1_out_38), .out_39(main_machine_1_out_39), .out_40(main_machine_1_out_40),
    .out_41(main_machine_1_out_41), .out_42(main_machine_1_out_42), .out_43(main_machine_1_out_43),
    .out_44(main_machine_1_out_44), .out_45(main_machine_1_out_45), .out_46(main_machine_1_out_46),
    .out_47(main_machine_1_out_47), .out_48(main_machine_1_out_48), .out_49(main_machine_1_out_49),
    .out_50(main_machine_1_out_50), .out_51(main_machine_1_out_51), .out_52(main_machine_1_out_52),
    .out_53(main_machine_1_out_53), .out_54(main_machine_1_out_54), .out_55(main_machine_1_out_55),
    .out_56(main_machine_1_out_56), .out_57(main_machine_1_out_57), .out_58(main_machine_1_out_58),
    .out_59(main_machine_1_out_59), .out_60(main_machine_1_out_60), .out_61(main_machine_1_out_61),
    .out_62(main_machine_1_out_62), .out_63(main_machine_1_out_63), .out_64(main_machine_1_out_64),
    .out_65(main_machine_1_out_65), .out_66(main_machine_1_out_66), .out_67(main_machine_1_out_67),
    .MEMORY_ADDRESS(main_machine_1_memory_address), .DATA_FROM_MEMORY(rom_1_data));  // open: out_3
  DotMatrix #(.matrixcols(32)) dotmatrix_1 (
    .col0(main_machine_1_out_4), .col1(main_machine_1_out_5), .col2(main_machine_1_out_6),
    .col3(main_machine_1_out_7), .col4(main_machine_1_out_8), .col5(main_machine_1_out_9),
    .col6(main_machine_1_out_10), .col7(main_machine_1_out_11), .col8(main_machine_1_out_12),
    .col9(main_machine_1_out_13), .col10(main_machine_1_out_14), .col11(main_machine_1_out_15),
    .col12(main_machine_1_out_16), .col13(main_machine_1_out_17), .col14(main_machine_1_out_18),
    .col15(main_machine_1_out_19), .col16(main_machine_1_out_20), .col17(main_machine_1_out_21),
    .col18(main_machine_1_out_22), .col19(main_machine_1_out_23), .col20(main_machine_1_out_24),
    .col21(main_machine_1_out_25), .col22(main_machine_1_out_26), .col23(main_machine_1_out_27),
    .col24(main_machine_1_out_28), .col25(main_machine_1_out_29), .col26(main_machine_1_out_30),
    .col27(main_machine_1_out_31), .col28(main_machine_1_out_32), .col29(main_machine_1_out_33),
    .col30(main_machine_1_out_34), .col31(main_machine_1_out_35));
  DotMatrix #(.matrixcols(32)) dotmatrix_2 (
    .col0(main_machine_1_out_36), .col1(main_machine_1_out_37), .col2(main_machine_1_out_38),
    .col3(main_machine_1_out_39), .col4(main_machine_1_out_40), .col5(main_machine_1_out_41),
    .col6(main_machine_1_out_42), .col7(main_machine_1_out_43), .col8(main_machine_1_out_44),
    .col9(main_machine_1_out_45), .col10(main_machine_1_out_46), .col11(main_machine_1_out_47),
    .col12(main_machine_1_out_48), .col13(main_machine_1_out_49), .col14(main_machine_1_out_50),
    .col15(main_machine_1_out_51), .col16(main_machine_1_out_52), .col17(main_machine_1_out_53),
    .col18(main_machine_1_out_54), .col19(main_machine_1_out_55), .col20(main_machine_1_out_56),
    .col21(main_machine_1_out_57), .col22(main_machine_1_out_58), .col23(main_machine_1_out_59),
    .col24(main_machine_1_out_60), .col25(main_machine_1_out_61), .col26(main_machine_1_out_62),
    .col27(main_machine_1_out_63), .col28(main_machine_1_out_64), .col29(main_machine_1_out_65),
    .col30(main_machine_1_out_66), .col31(main_machine_1_out_67));
  ROM #(.addrWidth(17)) rom_1 (.addr(main_machine_1_memory_address), .data(rom_1_data));  // open: sel

  // Notes on the sheet:
  //   ON OFF BUTTON
  //   UPLOAD GENERATED FILE HERE
  //   contents of rom_1 (hex, n*v repeats v):
  //   7f 8 8 8 7f 0 7f 49 49 41 41 0 7e 4*1 0 7e 4*1 0 3e 41 41 41 3e 0 0 d d e 8*0 41 41 7f 41 41 7*0 3f
  //   48 48 48 3f 0 7f 20 18 20 7f 7*0 3a 49 49 49 2e 0 3e 41 41 41 3e 0 7e 1 1 1 7e 0 7f 48 4c 4a 31 0 3f
  //   48 48 48 3f 0 3a 49 49 49 2e 0 7f 8 8 8 7f 0 41 41 7f 41 41 0 3a 49 49 49 2e 7*0 7f 41 41 41 3e 0 3f
  //   48 48 48 3f 0 3a 49 49 49 2e 0 1 130920*0 ba
endmodule

module reverse_register (
  input  [6:0] in_1,
  input  CLK,
  input  CLR,
  output [6:0] out_4
);

  Register #(.width(7)) register_1 (.D(in_1), .Q(out_4), .clk(CLK), .clr(CLR));  // open: en
endmodule

module display_buffer (
  input  [6:0] in_1,
  input  CLK,
  input  CLR,
  output [6:0] out_4,
  output [6:0] out_5,
  output [6:0] out_6,
  output [6:0] out_7,
  output [6:0] out_8,
  output [6:0] out_9,
  output [6:0] out_10,
  output [6:0] out_11,
  output [6:0] out_12,
  output [6:0] out_13,
  output [6:0] out_14,
  output [6:0] out_15,
  output [6:0] out_16,
  output [6:0] out_17,
  output [6:0] out_18,
  output [6:0] out_19,
  output [6:0] out_20,
  output [6:0] out_21,
  output [6:0] out_22,
  output [6:0] out_23,
  output [6:0] out_24,
  output [6:0] out_25,
  output [6:0] out_26,
  output [6:0] out_27,
  output [6:0] out_28,
  output [6:0] out_29,
  output [6:0] out_30,
  output [6:0] out_31,
  output [6:0] out_32,
  output [6:0] out_33,
  output [6:0] out_34,
  output [6:0] out_35,
  output [6:0] out_36,
  output [6:0] out_37,
  output [6:0] out_38,
  output [6:0] out_39,
  output [6:0] out_40,
  output [6:0] out_41,
  output [6:0] out_42,
  output [6:0] out_43,
  output [6:0] out_44,
  output [6:0] out_45,
  output [6:0] out_46,
  output [6:0] out_47,
  output [6:0] out_48,
  output [6:0] out_49,
  output [6:0] out_50,
  output [6:0] out_51,
  output [6:0] out_52,
  output [6:0] out_53,
  output [6:0] out_54,
  output [6:0] out_55,
  output [6:0] out_56,
  output [6:0] out_57,
  output [6:0] out_58,
  output [6:0] out_59,
  output [6:0] out_60,
  output [6:0] out_61,
  output [6:0] out_62,
  output [6:0] out_63,
  output [6:0] out_64,
  output [6:0] out_65,
  output [6:0] out_66,
  output [6:0] out_67,
  output [6:0] out_68
);

  reverse_register reverse_register_1 (.out_4(out_4), .CLK(CLK), .CLR(CLR), .in_1(out_5));
  reverse_register reverse_register_2 (.out_4(out_5), .CLK(CLK), .CLR(CLR), .in_1(out_6));
  reverse_register reverse_register_3 (.out_4(out_6), .CLK(CLK), .CLR(CLR), .in_1(out_7));
  reverse_register reverse_register_4 (.out_4(out_7), .CLK(CLK), .CLR(CLR), .in_1(out_8));
  reverse_register reverse_register_5 (.out_4(out_10), .CLK(CLK), .CLR(CLR), .in_1(out_11));
  reverse_register reverse_register_6 (.out_4(out_9), .CLK(CLK), .CLR(CLR), .in_1(out_10));
  reverse_register reverse_register_7 (.out_4(out_8), .CLK(CLK), .CLR(CLR), .in_1(out_9));
  reverse_register reverse_register_8 (.out_4(out_11), .CLK(CLK), .CLR(CLR), .in_1(out_12));
  reverse_register reverse_register_9 (.out_4(out_12), .CLK(CLK), .CLR(CLR), .in_1(out_13));
  reverse_register reverse_register_10 (.out_4(out_15), .CLK(CLK), .CLR(CLR), .in_1(out_16));
  reverse_register reverse_register_11 (.out_4(out_14), .CLK(CLK), .CLR(CLR), .in_1(out_15));
  reverse_register reverse_register_12 (.out_4(out_13), .CLK(CLK), .CLR(CLR), .in_1(out_14));
  reverse_register reverse_register_13 (.out_4(out_17), .CLK(CLK), .CLR(CLR), .in_1(out_18));
  reverse_register reverse_register_14 (.out_4(out_16), .CLK(CLK), .CLR(CLR), .in_1(out_17));
  reverse_register reverse_register_15 (.out_4(out_18), .CLK(CLK), .CLR(CLR), .in_1(out_19));
  reverse_register reverse_register_16 (.out_4(out_19), .CLK(CLK), .CLR(CLR), .in_1(out_20));
  reverse_register reverse_register_17 (.out_4(out_20), .CLK(CLK), .CLR(CLR), .in_1(out_21));
  reverse_register reverse_register_18 (.out_4(out_21), .CLK(CLK), .CLR(CLR), .in_1(out_22));
  reverse_register reverse_register_19 (.out_4(out_23), .CLK(CLK), .CLR(CLR), .in_1(out_24));
  reverse_register reverse_register_20 (.out_4(out_22), .CLK(CLK), .CLR(CLR), .in_1(out_23));
  reverse_register reverse_register_21 (.out_4(out_26), .CLK(CLK), .CLR(CLR), .in_1(out_27));
  reverse_register reverse_register_22 (.out_4(out_25), .CLK(CLK), .CLR(CLR), .in_1(out_26));
  reverse_register reverse_register_23 (.out_4(out_24), .CLK(CLK), .CLR(CLR), .in_1(out_25));
  reverse_register reverse_register_24 (.out_4(out_28), .CLK(CLK), .CLR(CLR), .in_1(out_29));
  reverse_register reverse_register_25 (.out_4(out_27), .CLK(CLK), .CLR(CLR), .in_1(out_28));
  reverse_register reverse_register_26 (.out_4(out_30), .CLK(CLK), .CLR(CLR), .in_1(out_31));
  reverse_register reverse_register_27 (.out_4(out_31), .CLK(CLK), .CLR(CLR), .in_1(out_32));
  reverse_register reverse_register_28 (.out_4(out_29), .CLK(CLK), .CLR(CLR), .in_1(out_30));
  reverse_register reverse_register_29 (.out_4(out_33), .CLK(CLK), .CLR(CLR), .in_1(out_34));
  reverse_register reverse_register_30 (.out_4(out_32), .CLK(CLK), .CLR(CLR), .in_1(out_33));
  reverse_register reverse_register_31 (.out_4(out_34), .CLK(CLK), .CLR(CLR), .in_1(out_35));
  reverse_register reverse_register_32 (.out_4(out_35), .CLK(CLK), .CLR(CLR), .in_1(out_36));
  reverse_register reverse_register_33 (.out_4(out_36), .CLK(CLK), .CLR(CLR), .in_1(out_37));
  reverse_register reverse_register_34 (.out_4(out_39), .CLK(CLK), .CLR(CLR), .in_1(out_40));
  reverse_register reverse_register_35 (.out_4(out_38), .CLK(CLK), .CLR(CLR), .in_1(out_39));
  reverse_register reverse_register_36 (.out_4(out_37), .CLK(CLK), .CLR(CLR), .in_1(out_38));
  reverse_register reverse_register_37 (.out_4(out_40), .CLK(CLK), .CLR(CLR), .in_1(out_41));
  reverse_register reverse_register_38 (.out_4(out_42), .CLK(CLK), .CLR(CLR), .in_1(out_43));
  reverse_register reverse_register_39 (.out_4(out_41), .CLK(CLK), .CLR(CLR), .in_1(out_42));
  reverse_register reverse_register_40 (.out_4(out_44), .CLK(CLK), .CLR(CLR), .in_1(out_45));
  reverse_register reverse_register_41 (.out_4(out_43), .CLK(CLK), .CLR(CLR), .in_1(out_44));
  reverse_register reverse_register_42 (.out_4(out_46), .CLK(CLK), .CLR(CLR), .in_1(out_47));
  reverse_register reverse_register_43 (.out_4(out_47), .CLK(CLK), .CLR(CLR), .in_1(out_48));
  reverse_register reverse_register_44 (.out_4(out_45), .CLK(CLK), .CLR(CLR), .in_1(out_46));
  reverse_register reverse_register_45 (.out_4(out_49), .CLK(CLK), .CLR(CLR), .in_1(out_50));
  reverse_register reverse_register_46 (.out_4(out_50), .CLK(CLK), .CLR(CLR), .in_1(out_51));
  reverse_register reverse_register_47 (.out_4(out_48), .CLK(CLK), .CLR(CLR), .in_1(out_49));
  reverse_register reverse_register_48 (.out_4(out_51), .CLK(CLK), .CLR(CLR), .in_1(out_52));
  reverse_register reverse_register_49 (.out_4(out_52), .CLK(CLK), .CLR(CLR), .in_1(out_53));
  reverse_register reverse_register_50 (.out_4(out_53), .CLK(CLK), .CLR(CLR), .in_1(out_54));
  reverse_register reverse_register_51 (.out_4(out_54), .CLK(CLK), .CLR(CLR), .in_1(out_55));
  reverse_register reverse_register_52 (.out_4(out_55), .CLK(CLK), .CLR(CLR), .in_1(out_56));
  reverse_register reverse_register_53 (.out_4(out_56), .CLK(CLK), .CLR(CLR), .in_1(out_57));
  reverse_register reverse_register_54 (.out_4(out_58), .CLK(CLK), .CLR(CLR), .in_1(out_59));
  reverse_register reverse_register_55 (.out_4(out_57), .CLK(CLK), .CLR(CLR), .in_1(out_58));
  reverse_register reverse_register_56 (.out_4(out_60), .CLK(CLK), .CLR(CLR), .in_1(out_61));
  reverse_register reverse_register_57 (.out_4(out_59), .CLK(CLK), .CLR(CLR), .in_1(out_60));
  reverse_register reverse_register_58 (.out_4(out_63), .CLK(CLK), .CLR(CLR), .in_1(out_64));
  reverse_register reverse_register_59 (.out_4(out_62), .CLK(CLK), .CLR(CLR), .in_1(out_63));
  reverse_register reverse_register_60 (.out_4(out_61), .CLK(CLK), .CLR(CLR), .in_1(out_62));
  reverse_register reverse_register_61 (.out_4(out_66), .CLK(CLK), .CLR(CLR), .in_1(out_67));
  reverse_register reverse_register_62 (.out_4(out_65), .CLK(CLK), .CLR(CLR), .in_1(out_66));
  reverse_register reverse_register_63 (.out_4(out_64), .CLK(CLK), .CLR(CLR), .in_1(out_65));
  reverse_register reverse_register_64 (.out_4(out_67), .CLK(CLK), .CLR(CLR), .in_1(out_68));
  reverse_register reverse_register_65 (.out_4(out_68), .CLK(CLK), .CLR(CLR), .in_1(in_1));
endmodule

module is_all_0 (
  input  [16:0] INPUT_DATA,
  output IS_ALL_BIT_0
);

  wire or_1_out;

  or or_1 (or_1_out, INPUT_DATA[0], INPUT_DATA[1], INPUT_DATA[2], INPUT_DATA[3], INPUT_DATA[4], INPUT_DATA[5], INPUT_DATA[6], INPUT_DATA[7], INPUT_DATA[8], INPUT_DATA[9], INPUT_DATA[10], INPUT_DATA[11], INPUT_DATA[12], INPUT_DATA[13], INPUT_DATA[14], INPUT_DATA[15], INPUT_DATA[16]);
  not not_1 (IS_ALL_BIT_0, or_1_out);
endmodule

module on_off_module (
  input  CLK,
  input  BUTTON,
  output INDICATOR,
  output CLK_OUTPUT
);

  T_Flip_Flop t_ff_1 (.clk(BUTTON), .T(BUTTON), .Q(INDICATOR));  // open: Qn, preset, reset, en
  Multiplexer #(.enable("false")) multiplexer_1 (.in0(1'b0), .in1(CLK), .out(CLK_OUTPUT), .sel(INDICATOR));
endmodule

module address_limit_register (
  input  [7:0] DATA_FROM_MEMORY,
  input  CLK,
  input  RESET,
  output [16:0] ADDRESS_LIMIT
);

  wire controlled_buffer_1_out, is_all_0_1_is_all_bit_0, not_1_out, or_1_out, t_ff_1_q;
  wire [7:0] register_1_q, register_2_q;
  wire [16:0] counter_1_q;
  wire [23:16] register_3_q;

  not not_1 (not_1_out, RESET);
  assign controlled_buffer_1_out = t_ff_1_q ? CLK : 1'bz;  // Controlled_Buffer controlled_buffer_1
  or or_1 (or_1_out, RESET, controlled_buffer_1_out);
  T_Flip_Flop t_ff_1 (
    .clk(is_all_0_1_is_all_bit_0), .T(is_all_0_1_is_all_bit_0), .Q(t_ff_1_q), .preset(RESET));  // open: Qn, reset, en
  is_all_0 is_all_0_1 (.INPUT_DATA(counter_1_q), .IS_ALL_BIT_0(is_all_0_1_is_all_bit_0));
  Counter #(.width(17), .max('h1ffff)) counter_1 (
    .load(1'b1), .D(17'h3), .count(not_1_out), .Q(counter_1_q), .clk(or_1_out));  // open: carry, clr
  Register register_1 (.D(DATA_FROM_MEMORY), .Q(register_1_q), .clk(controlled_buffer_1_out));  // open: en, clr
  Register register_2 (.D(register_1_q), .Q(register_2_q), .clk(controlled_buffer_1_out));  // open: en, clr
  Register register_3 (.D(register_2_q), .Q(register_3_q), .clk(controlled_buffer_1_out));  // open: en, clr
  Bit_Extender #(.in_width(24), .out_width(17)) bit_extender_1 (
    .in({register_3_q, register_2_q, register_1_q}), .out(ADDRESS_LIMIT));

  // Notes on the sheet:
  //   count for 3 registers
  //   can increment registers here
endmodule

module main_machine (
  input  ON_OFF_BUTTON,
  input  [7:0] DATA_FROM_MEMORY,
  output [6:0] out_3,
  output [6:0] out_4,
  output [6:0] out_5,
  output [6:0] out_6,
  output [6:0] out_7,
  output [6:0] out_8,
  output [6:0] out_9,
  output [6:0] out_10,
  output [6:0] out_11,
  output [6:0] out_12,
  output [6:0] out_13,
  output [6:0] out_14,
  output [6:0] out_15,
  output [6:0] out_16,
  output [6:0] out_17,
  output [6:0] out_18,
  output [6:0] out_19,
  output [6:0] out_20,
  output [6:0] out_21,
  output [6:0] out_22,
  output [6:0] out_23,
  output [6:0] out_24,
  output [6:0] out_25,
  output [6:0] out_26,
  output [6:0] out_27,
  output [6:0] out_28,
  output [6:0] out_29,
  output [6:0] out_30,
  output [6:0] out_31,
  output [6:0] out_32,
  output [6:0] out_33,
  output [6:0] out_34,
  output [6:0] out_35,
  output [6:0] out_36,
  output [6:0] out_37,
  output [6:0] out_38,
  output [6:0] out_39,
  output [6:0] out_40,
  output [6:0] out_41,
  output [6:0] out_42,
  output [6:0] out_43,
  output [6:0] out_44,
  output [6:0] out_45,
  output [6:0] out_46,
  output [6:0] out_47,
  output [6:0] out_48,
  output [6:0] out_49,
  output [6:0] out_50,
  output [6:0] out_51,
  output [6:0] out_52,
  output [6:0] out_53,
  output [6:0] out_54,
  output [6:0] out_55,
  output [6:0] out_56,
  output [6:0] out_57,
  output [6:0] out_58,
  output [6:0] out_59,
  output [6:0] out_60,
  output [6:0] out_61,
  output [6:0] out_62,
  output [6:0] out_63,
  output [6:0] out_64,
  output [6:0] out_65,
  output [6:0] out_66,
  output [6:0] out_67,
  output INDICATOR,
  output [16:0] MEMORY_ADDRESS
);

  wire clk, clock_1_out, comparator_1_eq, not_1_out, or_1_out;
  wire [6:0] bit_extender_1_out;
  wire [16:0] address_limit_register_1_address_limit;

  Clock clock_1 (.out(clock_1_out));
  on_off_module on_off_module_1 (.CLK(clock_1_out), .BUTTON(ON_OFF_BUTTON), .INDICATOR(INDICATOR), .CLK_OUTPUT(clk));
  Counter #(.width(17), .max('h1ffff)) counter_1 (
    .load(ON_OFF_BUTTON), .D(17'h1fffd), .count(not_1_out), .Q(MEMORY_ADDRESS), .clk(or_1_out),
    .clr(comparator_1_eq));  // open: carry
  not not_1 (not_1_out, ON_OFF_BUTTON);
  or or_1 (or_1_out, ON_OFF_BUTTON, clk);
  Comparator #(.width(17)) comparator_1 (
    .a(MEMORY_ADDRESS), .b(address_limit_register_1_address_limit), .eq(comparator_1_eq));  // open: gt, lt
  address_limit_register address_limit_register_1 (
    .CLK(clk), .RESET(ON_OFF_BUTTON), .ADDRESS_LIMIT(address_limit_register_1_address_limit),
    .DATA_FROM_MEMORY(DATA_FROM_MEMORY));
  display_buffer display_buffer_1 (
    .CLK(clk), .CLR(ON_OFF_BUTTON), .out_4(out_3), .out_5(out_4), .out_6(out_5), .out_7(out_6),
    .out_8(out_7), .out_9(out_8), .out_10(out_9), .out_11(out_10), .out_12(out_11), .out_13(out_12),
    .out_14(out_13), .out_15(out_14), .out_16(out_15), .out_17(out_16), .out_18(out_17), .out_19(out_18),
    .out_20(out_19), .out_21(out_20), .out_22(out_21), .out_23(out_22), .out_24(out_23), .out_25(out_24),
    .out_26(out_25), .out_27(out_26), .out_28(out_27), .out_29(out_28), .out_30(out_29), .out_31(out_30),
    .out_32(out_31), .out_33(out_32), .out_34(out_33), .out_35(out_34), .out_36(out_35), .out_37(out_36),
    .out_38(out_37), .out_39(out_38), .out_40(out_39), .out_41(out_40), .out_42(out_41), .out_43(out_42),
    .out_44(out_43), .out_45(out_44), .out_46(out_45), .out_47(out_46), .out_48(out_47), .out_49(out_48),
    .out_50(out_49), .out_51(out_50), .out_52(out_51), .out_53(out_52), .out_54(out_53), .out_55(out_54),
    .out_56(out_55), .out_57(out_56), .out_58(out_57), .out_59(out_58), .out_60(out_59), .out_61(out_60),
    .out_62(out_61), .out_63(out_62), .out_64(out_63), .out_65(out_64), .out_66(out_65), .out_67(out_66),
    .out_68(out_67), .in_1(bit_extender_1_out));
  Bit_Extender #(.out_width(7)) bit_extender_1 (.in(DATA_FROM_MEMORY), .out(bit_extender_1_out));

  // Notes on the sheet:
  //   address where the address limit is stored
endmodule
